# Fritzing sketch Trucky_Schema (saved by Fritzing 0.9.3b)
circuit board: 13.8912cm x 8.42259cm
breadboards: 1

parts:
  L293D = L293D [package=THT]
  VCC1 = Battery
  Front_Light_2 = smd LED [color="White (4500K)" package="1206 [SMD]"]
  Brake_Led_1 = smd LED [color="Red (635nm)" package="1206 [SMD]"]
  Brake_Led_2 = smd LED [color="Red (635nm)" package="1206 [SMD]"]
  Warning_Led_1 = smd LED [color="Yellow (585nm)" package="1206 [SMD]"]
  Warning_Led_2 = smd LED [color="Yellow (585nm)" package="1206 [SMD]"]
  Front_Light_1 = smd LED [color="White (4500K)" package="1206 [SMD]"]
  R1 = Resistor [tolerance=±5% resistance=220k package=THT]
  R2 = Resistor [tolerance=±5% resistance=220k package=THT]
  R3 = Resistor [tolerance=±5% resistance=220k package=THT]
  R4 = Resistor [tolerance=±5% resistance=220k package=THT]
  R5 = Resistor [tolerance=±5% resistance=220k package=THT]
  R6 = Resistor [tolerance=±5% resistance=220k package=THT]
  HM-10 = Bluetooth HC-05 Macho
  VCC2 = Battery
  Motor_Left = DC Motor
  Motor_Right = DC Motor
  Arduino_Nano = Arduino Nano (Rev3.0)

nets:
  VCC: L293D.Enable_1, L293D.Enable_2, L293D.+V, HM-10.VCC, Arduino_Nano.5V
  N1: L293D.In_1, Arduino_Nano.D11/MOSI
  N2: L293D.Out_1_(_Controlled_by_Enable_1_), Motor_Left.pin_2
  GND: L293D.0V, VCC1.-, R1.Pin_0, R2.Pin_0, R3.Pin_0, R4.Pin_0, R5.Pin_0, R6.Pin_0, HM-10.GND, Arduino_Nano.GND
  N3: L293D.Out_2_(_Controlled_by_Enable_1_), Motor_Left.pin_1
  N4: L293D.In_2, Arduino_Nano.D10
  N5: L293D.+Vmotor, VCC2.+, Arduino_Nano.VIN
  N6: L293D.In_3, Arduino_Nano.D6
  N7: L293D.Out_3_(_Controlled_by_Enable_2_), Motor_Right.pin_1
  N8: L293D.Out_4_(_Controlled_by_Enable_2_), Motor_Right.pin_2
  N9: L293D.In_4, Arduino_Nano.D9
  N10: VCC1.+, VCC2.-
  N11: Front_Light_2.cathode, Front_Light_1.cathode, Arduino_Nano.D3
  N12: Front_Light_2.anode, R2.Pin_1
  N13: Brake_Led_1.cathode, Brake_Led_2.cathode, Arduino_Nano.D4
  N14: Brake_Led_1.anode, R3.Pin_1
  N15: Brake_Led_2.anode, R4.Pin_1
  N16: Warning_Led_1.cathode, Warning_Led_2.cathode, Arduino_Nano.D13/SCK
  N17: Warning_Led_1.anode, R5.Pin_1
  N18: Warning_Led_2.anode, R6.Pin_1
  N19: Front_Light_1.anode, R1.Pin_1
  N20: HM-10.RXD, Arduino_Nano.D2

// code stored in the sketch: engines.ino

/*
* Engines Component
*/

/*
ARDUINO   L293D(Puente H)        
  10         2
  11         7
  10         6
  9          15
  5V         1, 9, 16
  GND        4, 5, 12, 13
  
  El motor LEFT se conecta a los pines 3 y 6 del Puente H
  El motor RIGHT se conecta a los pines 11 y 14 del Puente H
  
  La fuente de alimentacion de los Motores se conecta a tierra y
  el positivo al pin 8 del puente H.  

*/

//RIGHT Engine 
int rA = 8; 
int rB = 10; 
//LEFT Engine
int lA = 11; 
int lB = 6;

//
int prevThrottle = 49;
int prevSteering = 49;
int throttle, steering, Speed;

void enginesSetup()  { 
  pinMode(rA, OUTPUT);
  pinMode(rB, OUTPUT);
  pinMode(lA, OUTPUT);
  pinMode(lB, OUTPUT);
  Serial.begin(9600);
  analogWrite(rA, 0); 
  analogWrite(rB, 0);
  analogWrite(lA, 0); 
  analogWrite(lB, 0);
  
  Serial.println("Engines Setup complete");
 } 
 
void enginesLoop()  {
  /**
   * Speed 
   * We use map() funtion to calculate the Speed
   * according to throttle value recibed
   * example: x = map( value_getted , fromMin , fromMax , toMin , toMax );
   */
  //Speed = 255;
  Speed = map( throttle , 50 , 100 , 0 , 255 );
  
  // Throttle and steering values go from 0 to 99.
  // When throttle and steering values are at 99/2 = 49, the joystick is at center.
  throttle = phone.getThrottle();
  steering = phone.getSteering();
  // Display throttle and steering data if steering or throttle value is changed
//  if (prevThrottle != throttle) {
//    Serial.print("Throttle: "); Serial.println(throttle) ; Serial.println(Speed);Serial.println(-Speed);
//  }
  
  //STOP  
  if (prevThrottle == throttle){
    analogWrite(rA, 0); 
    analogWrite(rB, 0);
    analogWrite(lA, 0); 
    analogWrite(lB, 0);   
  }    
//  //MOTOR left FORWARDS :::TURNS RIGHT
//  if (prevSteering != steering && prevSteering <= steering){
//      Serial.println("MOTOR left FORWARDS");
//      analogWrite(rA, 0); 
//      analogWrite(rB, 0);
//      analogWrite(lA, Speed); 
//      analogWrite(lB, 0);
//  }
//  //MOTOR right FORWARDS :::TURNS LEFT
//  if (prevSteering != steering && prevSteering >= steering){
//      Serial.println("MOTOR right FORWARDS");
//      analogWrite(rA, Speed); 
//      analogWrite(rB, 0);
//      analogWrite(lA, 0); 
//      analogWrite(lB, 0); 
//  }
      
  //MOTOR left & right FORWARDS
  if (prevThrottle != throttle && prevThrottle <= throttle){
      Serial.println("MOTOR left & right FORWARDS"); Serial.println(Speed);
      analogWrite(rA, Speed); 
      analogWrite(rB, 0);
      analogWrite(lA, Speed); 
      analogWrite(lB, 0); 
  }
  //MOTOR left & right BACKWARDS
  if (prevThrottle != throttle && prevThrottle >= throttle){
      Serial.println("MOTOR left & right BACKWARDS"); Serial.println(Speed);
      analogWrite(rA, 0); 
      analogWrite(rB, -Speed);
      analogWrite(lA, 0); 
      analogWrite(lB, -Speed); 
  }
}

// code stored in the sketch: lights.ino

/*
* Lights Component
*/

int button;
int timer = 100;

void lightsSetup() {

  // Loop to initialize each Light pin as an output:
  for (int thisPin = 4; thisPin < 6; thisPin++) {
    pinMode(thisPin, OUTPUT);
  }
  pinMode(13, OUTPUT);
  //Loop to initialize each Light pin OFF
  for (int thisPin = 4; thisPin < 6; thisPin++) {
    digitalWrite(thisPin, LOW);
  }
  digitalWrite(13, LOW);
  Serial.println("Lights Setup complete");
}

void lightsLoop() {
  // ID of the button pressed pressed.
  button = phone.getButton();
  
  // All lights on!
  if (button == 4) {
    for (int thisPin = 4; thisPin <= 5; thisPin++) {
      digitalWrite(thisPin, !digitalRead(thisPin));
    }
    digitalWrite(13, !digitalRead(13));
    Serial.println("Todas encendidas!");
  }
  // Front Lights
  if (button == 0) {
    digitalWrite(4, !digitalRead(4));
    Serial.println("Luces delanteras!");
    Serial.println(digitalRead(4));
  } 

  // Breaks
  if (button == 1) {
    digitalWrite(5, !digitalRead(5));
    Serial.println("Luces traseras!");
    Serial.println(digitalRead(5));
  }

  // Warning Lights
  if (button == 2) {
    digitalWrite(13, !digitalRead(13));
    Serial.println("Luces Advertencia!");
    Serial.println(digitalRead(13));
  }

  // All systems down!
//  if (button == 3) {
//    for (int thisPin = 2; thisPin <= 10; thisPin++) {
//      digitalWrite(thisPin, LOW);
//    }
//    Serial.println("Todas apagado!");
//  }
}

// code stored in the sketch: Trucky.ino

/*
* Trucky Project
*/

#include <SoftwareSerial.h>
#include <ArduinoBlue.h>


// The bluetooth tx and rx pins must be supported by software serial.
// Visit https://www.arduino.cc/en/Reference/SoftwareSerial for unsupported pins.
// Bluetooth TX -> Arduino D3
const int BLUETOOTH_TX = 3;
// Bluetooth RX -> Arduino D2
const int BLUETOOTH_RX = 2;

SoftwareSerial bluetooth(BLUETOOTH_TX, BLUETOOTH_RX);
ArduinoBlue phone(bluetooth); // pass reference of bluetooth object to ArduinoBlue constructor.


void setup() {
  // Start serial monitor at 9600 bps.
  Serial.begin(9600);

  // Start bluetooth serial at 9600 bps.
  bluetooth.begin(9600);
  bluetooth.write("AT+NAMEBLE_Trucky_Unit");

  lightsSetup();
  enginesSetup();

  // delay just in case bluetooth module needs time to "get ready".
  delay(100);

  Serial.println("Trucky Setup complete");
}

void loop() {
  lightsLoop();
  enginesLoop();
}
